# Fritzing sketch cohete (saved by Fritzing 1.0.1rc)
breadboards: 1

parts:
  SM1 = 28BYJ-48 Stepper Motor [part_number=28BYJ-48]
  Power_plug1 = Power plug
  Pico/Pico2_Mod_1 = Raspberry Pi Pico or Pico 2
  Mod1 = KY-009 Full Color RGB LED SMD Module [package="Breakout board"]
  Mod2 = KY-027 Magic Light Cup Module [package="Breakout board"]
  Mod3 = KY-026 Flame Sensor Module [package="Breakout board"]
  R1 = Resistor [tolerance=±5% power=0.25 resistance=220 package=THT]
  LED1 = LED - 5mm [color="Red (633nm)" current=0.030 package="5 mm [THT]"]
  R3 = Resistor [tolerance=±5% power=0.25 resistance=220 package=THT]
  R4 = Resistor [tolerance=±5% power=0.25 resistance=220 package=THT]
  R2 = Resistor [tolerance=±5% power=0.25 resistance=220 package=THT]
  Driver1 = 28BYJ-48 Driver Module [part_number=ULN2003 package=THT]

nets:
  N1: SM1.blue-pin, Driver1.blue-pin
  N2: SM1.pink-pin, Driver1.pink-pin
  N3: SM1.yellow-pin, Driver1.yellow-pin
  N4: SM1.orange-pin, Driver1.orange-pin
  N5: SM1.red-pin, Driver1.red-pin
  GND: Power_plug1.GND, Driver1.GND
  N6: Power_plug1.VCC, Driver1.Vmotor
  N7: Pico/Pico2_Mod_1.pin_3, Pico/Pico2_Mod_1.pin_8, Pico/Pico2_Mod_1.pin_13, Pico/Pico2_Mod_1.pin_18, Pico/Pico2_Mod_1.pin_23, Pico/Pico2_Mod_1.pin_28, Pico/Pico2_Mod_1.pin_33, Pico/Pico2_Mod_1.pin_38, Mod1.-, Mod2.G, Mod2.L, Mod3.G, LED1.anode
  N8: Pico/Pico2_Mod_1.pin_14, Driver1.IN1
  N9: Pico/Pico2_Mod_1.pin_15, Driver1.IN2
  N10: Pico/Pico2_Mod_1.pin_16, Driver1.IN3
  N11: Pico/Pico2_Mod_1.pin_17, Driver1.IN4
  N12: Pico/Pico2_Mod_1.pin_21, Mod3.D0
  N13: Pico/Pico2_Mod_1.pin_22, R1.Pin_1
  N14: Pico/Pico2_Mod_1.pin_24, R3.Pin_1
  N15: Pico/Pico2_Mod_1.pin_25, R4.Pin_1
  N16: Pico/Pico2_Mod_1.pin_26, R2.Pin_1
  N17: Pico/Pico2_Mod_1.pin_27, Mod2.S
  N18: Pico/Pico2_Mod_1.pin_31, Mod3.A0
  N19: Pico/Pico2_Mod_1.pin_36, Mod2.+, Mod3.+
  N20: Mod1.B, R2.Pin_0
  N21: Mod1.G, R4.Pin_0
  N22: Mod1.R, R3.Pin_0
  N23: R1.Pin_0, LED1.cathode

custom parts:
  28BYJ-48 Stepper Motor: Unipolar Stepper Motor 28BYJ-48 Top coil - pink & orange Bottom coil - blue & yellow Common rail - red Connector pins: blue - pink - yellow - orange - red
  Raspberry Pi Pico or Pico 2: Raspberry Pi Pico and Pico 2. Based around the RP2040 and RP2350 microcontrollers respectively, Picos are low cost microcontroller device bringing Raspberry Pi quality, cost, and easy of use to the microcontroller space. Jan 2021, Split part in to two versions: tht (this one) and SMD. This one will drill holes for a .1 in header in pcb to allow plugging in the module as well as providing pads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
  KY-009 Full Color RGB LED SMD Module: KY-009 RGB full color LED Module, emits a range of colors by mixing red, green and blue light. The amount of each color is adjusted using PWM.
  KY-027 Magic Light Cup Module: KY-0127 Magic Light Cup module is a set of two boards, each one has a led and a mercury tilt switch. Using PWM to drive the LEDs on each module you can achieve the effect of light being "magically" transferred from one module to the other when tilting them.
  KY-026 Flame Sensor Module: KY-026 Flame Sensor Module reacts in the presence of fire.
  28BYJ-48 Driver Module: ULN2003 Driver Module for the 28BYJ-48 Unipolar Stepper Motor LED A - Blue wire - Bottom coil left LED B - Pink wire - Top coil left LED C - Yellow wire - Bottom coil right LED D - Orange wire - Top coil right Common rail - red Connector pins: blue - pink - yellow - orange - red Control pins - IN1 to IN4 Power pins - GND & Vmotor (5-12V) On/Off jumper (if removed, power to motor is cut).
